# Fritzing sketch miniproject-fritzing (saved by Fritzing 0.9.4)
breadboards: 3

parts:
  元件2 = Adafruit ItsyBitsy M4 [part_number="Adafruit #3800"]
  hc-sr2 = hc-sr04
  TFT2 = 1.44" SPI TFT Graphics Display 128x128 [package=THT]
  U6 = 74HC595 [package="DIP16 [THT]"]
  C2 = Tantalum Capacitor [capacitance="1 μF" package="C 6032 [SMD, tantalum]"]
  KEYPAD2 = Membrane Matrix Keypad
  J2 = Piezo Speaker
  LED8 = LED - 5mm [color="Green (555nm)" package="5 mm [THT]"]
  LED9 = LED - 5mm [color="Green (565nm)" package="5 mm [THT]"]
  LED12 = LED - 5mm [color="Yellow (592nm)" package="5 mm [THT]"]
  LED13 = LED - 5mm [color="Yellow (592nm)" package="5 mm [THT]"]
  LED14 = LED - 5mm [color="Red (633nm)" package="5 mm [THT]"]
  LED15 = LED - 5mm [color="Red (633nm)" package="5 mm [THT]"]
  R11 = Resistor [tolerance=±20% resistance=1k package=THT]
  R12 = Resistor [tolerance=±20% resistance=1k package=THT]
  R13 = Resistor [tolerance=±20% resistance=1k package=THT]
  J3 = Basic Servo
  J4 = Basic Servo
  J5 = Basic Servo
  J6 = Basic Servo
  LED16 = LED - 5mm [color="Red (633nm)" package="5 mm [THT]"]

nets:
  N1: 元件2.D3, U6.ST_CP
  N2: 元件2.D4, KEYPAD2.1
  GND: 元件2.GND, hc-sr2.GND, TFT2.pin10, U6.GND, U6.OE, C2.-, J2.pin1, LED8.cathode, LED12.cathode, LED15.cathode, J3.gnd, J4.gnd, J5.gnd, J6.gnd
  N3: 元件2.D13, KEYPAD2.5
  N4: 元件2.D12, TFT2.pin2
  N5: 元件2.D11, KEYPAD2.6
  N6: 元件2.D10, TFT2.pin5, J6.pulse
  N7: 元件2.D9, J5.pulse
  N8: 元件2.D7, TFT2.pin4
  N9: 元件2.SCL, J4.pulse
  N10: 元件2.SDA, J3.pulse
  N11: 元件2.RX_D0, TFT2.pin3
  N12: 元件2.D2, KEYPAD2.7
  N13: 元件2.MISO, TFT2.pin7
  N14: 元件2.MOSI, TFT2.pin6, U6.DS
  N15: 元件2.SCK, TFT2.pin8, U6.SH_CP
  N16: 元件2.A5, hc-sr2.Echo
  N17: 元件2.A4, hc-sr2.Trig
  N18: 元件2.A3, KEYPAD2.3
  N19: 元件2.A2, KEYPAD2.2
  N20: 元件2.A1, J2.pin2
  N21: 元件2.A0, KEYPAD2.4
  VCC: 元件2.VHI, hc-sr2.VCC, J3.vcc, J4.vcc, J5.vcc, J6.vcc
  +3V3: 元件2.+3V3, TFT2.pin11, U6.MR, U6.VCC, C2.+
  N22: U6.Q5, R12.Pin_0
  N23: U6.Q6, R13.Pin_0
  N24: U6.Q7, R11.Pin_0
  N25: LED8.anode, LED9.cathode
  N26: LED9.anode, R11.Pin_1
  N27: LED12.anode, LED13.cathode
  N28: LED13.anode, R13.Pin_1
  N29: LED14.cathode, LED16.anode
  N30: LED14.anode, R12.Pin_1
  N31: LED15.anode, LED16.cathode

custom parts:
  Adafruit ItsyBitsy M4: What's smaller than a Feather but larger than a Trinket? It's an Adafruit ItsyBitsy M4 Express featuring the Microchip ATSAMD51! Small, powerful, with a ultra fast ATSAMD51 Cortex M4 processor running at 120 MHz - this microcontroller board is perfect when you want something very compact, with a ton of horsepower and a bunch of pins. This Itsy is like a bullet train, with it's 120MHz Cortex M4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
  1.44" SPI TFT Graphics Display 128x128: This is for https://www.amazon.com/gp/product/B07B4BDWCL/ref=ask_ql_qh_dp_hza display. Note that this display is sold with a misprinted silkscreen indicating I2C connections on P2 connector, it is actualy SPI. The P1 connections are non functional on this board from the linked URL seller on Amazon.
  Membrane Matrix Keypad: Membrane Matrix 3x4 Keypad
